// Logisim project ALU.circ as structural Verilog: 1 circuit, main circuit main
module main (
  input  [15:0] A,
  input  [15:0] B,
  input  [2:0] ALUCtr,
  output [15:0] C,
  output zero
);

  wire [15:0] adder_1_out, and_1_out, divider_1_out, multiplier_1_out, subtractor_1_out, xor_1_out;

  Adder #(.width(16)) adder_1 (.a(A), .b(B), .out(adder_1_out));  // open: cin, cout
  assign and_1_out = A & B;  // AND_Gate and_1, 16 bits wide
  Subtractor #(.width(16)) subtractor_1 (.a(A), .b(B), .out(subtractor_1_out));  // open: bin, bout
  Divider #(.width(16)) divider_1 (.a(A), .b(B), .out(divider_1_out));  // open: upper, rem
  Multiplier #(.width(16)) multiplier_1 (.a(A), .b(B), .out(multiplier_1_out));  // open: cin, cout
  assign xor_1_out = A ^ B;  // XOR_Gate xor_1, 16 bits wide
  Multiplexer #(.select(3), .width(16), .enable("false")) multiplexer_1 (
    .in0(adder_1_out), .in1(adder_1_out), .in2(and_1_out), .in4(subtractor_1_out), .in5(divider_1_out),
    .in6(multiplier_1_out), .in7(xor_1_out), .out(C), .sel(ALUCtr));  // open: in3
  Comparator #(.width(16)) comparator_1 (.a(C), .b({16{1'b0}}), .eq(zero));  // open: gt, lt

  // Notes on the sheet:
  //   SUB
  //   ADD
endmodule
