// Logisim project CPU.circ as structural Verilog: 1 circuit, main circuit main
module main (
  input  in_1
);

  wire ALU_zero, and_1_out, clock_1_out, main_1_alusrc, main_1_branch, main_1_memread, main_1_memtoreg,
       main_1_memwrite, main_1_regdst, main_1_regwrite;
  wire [2:0] main_1_aluop;
  wire [3:0] multiplexer_1_out, rom_1_data;
  wire [15:0] adder_1_out, ALU_c, main_2_data_reader_1, main_2_data_reader_2, multiplexer_2_out,
       multiplexer_3_out, multiplexer_4_out, Pc_q, ram_1_data;
  wire [31:4] rom_1_data_2;

  Clock clock_1 (.out(clock_1_out));
  Register #(.width(16)) Pc (.D(multiplexer_3_out), .Q(Pc_q), .clk(clock_1_out), .clr(in_1));  // open: en
  Control_Unit_main main_1 (
    .OP_Code(rom_1_data), .ALUOP(main_1_aluop), .RegDst(main_1_regdst), .ALUsrc(main_1_alusrc),
    .MemtoReg(main_1_memtoreg), .RegWrite(main_1_regwrite), .MemWrite(main_1_memwrite),
    .MemRead(main_1_memread), .Branch(main_1_branch));
  Adder #(.width(16)) adder_1 (.a(16'h1), .b(Pc_q), .out(adder_1_out));  // open: cin, cout
  ROM #(.addrWidth(16), .dataWidth(32)) rom_1 (.addr(Pc_q), .data({rom_1_data_2, rom_1_data}));  // open: sel
  Multiplexer #(.width(4), .disabled(0), .enable("false")) multiplexer_1 (
    .in0(rom_1_data_2[11:8]), .in1(rom_1_data_2[15:12]), .out(multiplexer_1_out), .sel(main_1_regdst));
  Register_File_main main_2 (
    .Data_Reader_1(main_2_data_reader_1), .Data_Reader_2(main_2_data_reader_2),
    .Register_Address_1(rom_1_data_2[7:4]), .Register_Address_2(rom_1_data_2[11:8]),
    .Data_writer(multiplexer_4_out), .Write_Address(multiplexer_1_out), .Write_Reg(main_1_regwrite),
    .Clock(clock_1_out));
  Multiplexer #(.width(16), .disabled(0), .enable("false")) multiplexer_2 (
    .in0(main_2_data_reader_2), .in1(rom_1_data_2[31:16]), .out(multiplexer_2_out), .sel(main_1_alusrc));
  and and_1 (and_1_out, main_1_branch, ~ALU_zero);  // AND_Gate
  ALU_main ALU (.A(main_2_data_reader_1), .B(multiplexer_2_out), .C(ALU_c), .zero(ALU_zero), .ALUCtr(main_1_aluop));
  Multiplexer #(.width(16), .disabled(0), .enable("false")) multiplexer_3 (
    .in0(adder_1_out), .in1(rom_1_data_2[31:16]), .out(multiplexer_3_out), .sel(and_1_out));
  RAM #(.addrWidth(16), .dataWidth(16), .bus("separate")) ram_1 (
    .addr(ALU_c), .din(main_2_data_reader_2), .data(ram_1_data), .str(main_1_memwrite), .clk(clock_1_out),
    .ld(main_1_memread));  // open: sel, clr
  Multiplexer #(.width(16), .disabled(0), .enable("false")) multiplexer_4 (
    .in0(ALU_c), .in1(ram_1_data), .out(multiplexer_4_out), .sel(main_1_memtoreg));

  // Notes on the sheet:
  //   contents of rom_1 (hex, n*v repeats v):
  //   11 10012 3333faff
endmodule
