// Logisim project Control_Unit.circ as structural Verilog: 1 circuit, main circuit main
module main (
  input  [3:0] OP_Code,
  output [2:0] ALUOP,
  output RegDst,
  output ALUsrc,
  output MemtoReg,
  output RegWrite,
  output MemWrite,
  output MemRead,
  output Branch
);

  wire ADD_out, AND_out, ANDI_out, DIV_out, MUL_out, SUB_out, XOR_out;

  and DIV (DIV_out, OP_Code[3], ~OP_Code[2], OP_Code[1], ~OP_Code[0]);  // AND_Gate
  and ADD (ADD_out, ~OP_Code[3], ~OP_Code[2], ~OP_Code[1], ~OP_Code[0]);  // AND_Gate
  and MUL (MUL_out, OP_Code[3], OP_Code[2], ~OP_Code[1], ~OP_Code[0]);  // AND_Gate
  and SUB (SUB_out, OP_Code[3], ~OP_Code[2], ~OP_Code[1], ~OP_Code[0]);  // AND_Gate
  and Bnq (Branch, OP_Code[3], ~OP_Code[2], ~OP_Code[1], OP_Code[0]);  // AND_Gate
  and AND (AND_out, ~OP_Code[3], OP_Code[2], ~OP_Code[1], ~OP_Code[0]);  // AND_Gate
  and LW (MemRead, ~OP_Code[3], ~OP_Code[2], ~OP_Code[1], OP_Code[0]);  // AND_Gate
  and SW (MemWrite, ~OP_Code[3], ~OP_Code[2], OP_Code[1], ~OP_Code[0]);  // AND_Gate
  and ANDI (ANDI_out, ~OP_Code[3], OP_Code[2], ~OP_Code[1], OP_Code[0]);  // AND_Gate
  and XOR (XOR_out, OP_Code[3], OP_Code[2], OP_Code[1], OP_Code[0]);
  or or_1 (RegDst, DIV_out, MUL_out, ADD_out, SUB_out, AND_out, XOR_out);
  or or_2 (ALUsrc, MemRead, MemWrite, ANDI_out);
  or or_3 (RegWrite, MUL_out, ADD_out, SUB_out, AND_out, MemRead, ANDI_out, XOR_out, DIV_out);

  assign ALUOP = OP_Code[3:1];
  assign MemtoReg = MemRead;
endmodule
